# Fritzing sketch minheating (saved by Fritzing 0.9.2b)
breadboards: 1

parts:
  U3 = G3VM-61E1 [package=g3vm-61e1]
  Componente1 = Arduino Uno (Rev3)
  Water_Pump = DC Motor [part_number="Change Hot Water from Solar Panel to Swimming Pool"]
  Power_plug1 = Power plug
  U4 = POT [package=pot_mammoth]

nets:
  N1: U3.P$1, Componente1.GND, U4.A
  N2: U3.P$2, Componente1.5V, U4.E
  N3: U3.P$3, Componente1.D7
  N4: U3.P$4, Water_Pump.pin_1
  N5: U3.P$5, Power_plug1.VCC
  N6: Componente1.A0, U4.S
  N7: Water_Pump.pin_2, Power_plug1.GND

notes:
  aquecimento
  VCC 127V
  Relays
